// Logisim project zajecia11.circ as structural Verilog: 5 circuits, main circuit main
module main (
  input  in_1,
  input  in_2,
  input  in_3,
  input  in_4,
  input  in_5
);

  wire clock_1_out, clock_2_out, clock_3_out, clock_4_out, demultiplexer_1_out_4, demultiplexer_1_out_5,
       demultiplexer_1_out_6, demultiplexer_1_out_7, multiplexer_nor_nand_1_out_7, nuclear_1_out_4;

  Clock clock_1 (.out(clock_1_out));
  Clock #(.highDuration(2)) clock_2 (.out(clock_2_out));
  Clock #(.lowDuration(2)) clock_3 (.out(clock_3_out));
  Clock #(.highDuration(2), .lowDuration(2)) clock_4 (.out(clock_4_out));
  LED led_1 (.in(nuclear_1_out_4));
  nuclear nuclear_1 (.A(in_1), .B(in_2), .C(in_3), .out_4(nuclear_1_out_4));
  multiplexer_nor_nand multiplexer_nor_nand_1 (
    .in_1(clock_1_out), .in_2(clock_2_out), .in_3(clock_3_out), .in_4(clock_4_out), .in_5(in_4), .in_6(in_5),
    .out_7(multiplexer_nor_nand_1_out_7));
  demultiplexer demultiplexer_1 (
    .in_1(multiplexer_nor_nand_1_out_7), .in_2(in_4), .in_3(in_5), .out_4(demultiplexer_1_out_4),
    .out_5(demultiplexer_1_out_5), .out_6(demultiplexer_1_out_6), .out_7(demultiplexer_1_out_7));
  LED led_2 (.in(demultiplexer_1_out_4));
  LED led_3 (.in(demultiplexer_1_out_5));
  LED led_4 (.in(clock_3_out));
  LED led_5 (.in(demultiplexer_1_out_6));
  LED led_6 (.in(clock_4_out));
  LED led_7 (.in(demultiplexer_1_out_7));
  LED led_8 (.in(clock_1_out));
  LED led_9 (.in(clock_2_out));
endmodule

// 1
module nuclear (
  input  A,
  input  B,
  input  C,
  output out_4
);

  wire nand_1_out, nand_2_out, nand_3_out;

  nand nand_1 (nand_1_out, A, B);
  nand nand_2 (nand_2_out, A, C);
  nand nand_3 (nand_3_out, B, C);
  nand nand_4 (out_4, nand_1_out, nand_2_out, nand_3_out);
endmodule

module multiplexer (
  input  in_1,
  input  in_2,
  input  in_3,
  input  in_4,
  input  in_5,
  input  in_6,
  output out_7
);

  wire and_1_out, and_2_out, and_3_out, and_4_out, not_1_out, not_2_out;

  not not_1 (not_1_out, in_5);
  not not_2 (not_2_out, in_6);
  and and_1 (and_1_out, in_1, not_1_out, not_2_out);
  and and_2 (and_2_out, in_2, not_1_out, in_6);
  and and_3 (and_3_out, in_3, in_5, in_6);
  and and_4 (and_4_out, in_4, in_5, in_6);
  or or_1 (out_7, and_1_out, and_2_out, and_3_out, and_4_out);
  LED led_1 (.in(out_7));
endmodule

module multiplexer_nor_nand (
  input  in_1,
  input  in_2,
  input  in_3,
  input  in_4,
  input  in_5,
  input  in_6,
  output out_7
);

  wire nand_1_out, nand_2_out, nand_3_out, nand_4_out, not_1_out, not_2_out;

  not not_1 (not_1_out, in_5);
  not not_2 (not_2_out, in_6);
  nand nand_1 (nand_1_out, in_1, not_1_out, not_2_out);
  nand nand_2 (nand_2_out, in_2, not_1_out, in_6);
  nand nand_3 (nand_3_out, in_3, in_5, not_2_out);
  nand nand_4 (nand_4_out, in_4, in_5, in_6);
  nand nand_5 (out_7, nand_1_out, nand_2_out, nand_3_out, nand_4_out);
  LED led_1 (.in(out_7));
endmodule

module demultiplexer (
  input  in_1,
  input  in_2,
  input  in_3,
  output out_4,
  output out_5,
  output out_6,
  output out_7
);

  wire not_1_out, not_2_out, not_3_out;

  not not_1 (not_1_out, in_1);
  not not_2 (not_2_out, in_2);
  not not_3 (not_3_out, in_3);
  nor nor_1 (out_4, not_1_out, in_2, in_3);
  nor nor_2 (out_5, not_1_out, in_2, not_3_out);
  nor nor_3 (out_6, not_1_out, not_2_out, in_3);
  nor nor_4 (out_7, not_1_out, not_3_out, not_2_out);
endmodule
